// Logisim project Projeto.circ as structural Verilog
module \Dário  (
  input  in_1,
  input  [7:0] in_2,
  output [7:0] out_3
);

  wire and_1_out, and_2_out, and_3_out, and_4_out, and_5_out, and_6_out, and_7_out, and_8_out, and_9_out,
       and_10_out, and_11_out, and_12_out, and_13_out, and_14_out, and_15_out, and_16_out, and_17_out,
       and_18_out, and_19_out, and_20_out, and_21_out, and_22_out, and_23_out, and_24_out, and_25_out,
       and_26_out, and_27_out, and_31_out, and_32_out, and_33_out, and_34_out, and_35_out, and_36_out,
       and_37_out, and_38_out, and_39_out, not_1_out, not_2_out, not_3_out, not_4_out, not_5_out, not_6_out,
       not_7_out, not_8_out, not_9_out, not_10_out, not_11_out, not_12_out, not_13_out, not_14_out,
       not_15_out, not_16_out, pulso2, pulso4, pulso6, pulso8, Setter;

  not not_1 (not_1_out, out_3[0]);
  and and_1 (and_1_out, 1'b1, not_1_out);
  and and_2 (and_2_out, 1'b1, out_3[0]);
  and and_3 (and_3_out, in_2[0], Setter);
  not not_2 (not_2_out, in_2[0]);
  not not_3 (not_3_out, out_3[2]);
  and and_4 (and_4_out, pulso2, not_3_out);
  and and_5 (and_5_out, out_3[2], pulso2);
  and and_6 (and_6_out, in_2[2], Setter);
  not not_4 (not_4_out, in_2[2]);
  not not_5 (not_5_out, out_3[4]);
  and and_7 (and_7_out, pulso4, not_5_out);
  and and_8 (and_8_out, out_3[4], pulso4);
  and and_9 (and_9_out, in_2[4], Setter);
  not not_6 (not_6_out, in_2[4]);
  J_K_Flip_Flop j_k_ff_1 (
    .J(and_1_out), .clk(in_1), .K(and_2_out), .Q(out_3[0]), .preset(and_3_out), .reset(and_10_out));  // open: Qn, en
  and and_10 (and_10_out, not_2_out, Setter);
  J_K_Flip_Flop j_k_ff_2 (
    .J(and_4_out), .clk(in_1), .K(and_5_out), .Q(out_3[2]), .preset(and_6_out), .reset(and_11_out));  // open: Qn, en
  and and_11 (and_11_out, not_4_out, Setter);
  J_K_Flip_Flop j_k_ff_3 (
    .J(and_7_out), .clk(in_1), .K(and_8_out), .Q(out_3[4]), .preset(and_9_out), .reset(and_12_out));  // open: Qn, en
  and and_12 (and_12_out, not_6_out, Setter);
  and and_13 (and_13_out, 1'b1, out_3[0]);
  not not_7 (not_7_out, out_3[1]);
  and and_14 (and_14_out, and_13_out, not_7_out);
  and and_15 (and_15_out, out_3[1], and_13_out);
  and and_16 (and_16_out, pulso2, out_3[2]);
  not not_8 (not_8_out, out_3[3]);
  and and_17 (and_17_out, and_16_out, not_8_out);
  and and_18 (and_18_out, pulso4, out_3[4]);
  not not_9 (not_9_out, out_3[5]);
  and and_19 (and_19_out, and_18_out, not_9_out);
  J_K_Flip_Flop j_k_ff_4 (
    .J(and_14_out), .clk(in_1), .K(and_15_out), .Q(out_3[1]), .preset(and_20_out), .reset(and_21_out));  // open: Qn, en
  and and_20 (and_20_out, in_2[1], Setter);
  not not_10 (not_10_out, in_2[1]);
  and and_21 (and_21_out, not_10_out, Setter);
  and and_22 (and_22_out, out_3[3], and_16_out);
  J_K_Flip_Flop j_k_ff_5 (
    .J(and_17_out), .clk(in_1), .K(and_22_out), .Q(out_3[3]), .preset(and_23_out), .reset(and_24_out));  // open: Qn, en
  and and_23 (and_23_out, in_2[3], Setter);
  not not_11 (not_11_out, in_2[3]);
  and and_24 (and_24_out, not_11_out, Setter);
  and and_25 (and_25_out, out_3[5], and_18_out);
  J_K_Flip_Flop j_k_ff_6 (
    .J(and_19_out), .clk(in_1), .K(and_25_out), .Q(out_3[5]), .preset(and_26_out), .reset(and_27_out));  // open: Qn, en
  and and_26 (and_26_out, in_2[5], Setter);
  not not_12 (not_12_out, in_2[5]);
  and and_27 (and_27_out, not_12_out, Setter);
  and and_28 (pulso2, and_13_out, out_3[1]);
  and and_29 (pulso4, and_16_out, out_3[3]);
  and and_30 (pulso6, and_18_out, out_3[5]);
  not not_13 (not_13_out, out_3[6]);
  and and_31 (and_31_out, pulso6, not_13_out);
  and and_32 (and_32_out, out_3[6], pulso6);
  J_K_Flip_Flop j_k_ff_7 (
    .J(and_31_out), .clk(in_1), .K(and_32_out), .Q(out_3[6]), .preset(and_33_out), .reset(and_34_out));  // open: Qn, en
  and and_33 (and_33_out, in_2[6], Setter);
  not not_14 (not_14_out, in_2[6]);
  and and_34 (and_34_out, not_14_out, Setter);
  and and_35 (and_35_out, pulso6, out_3[6]);
  not not_15 (not_15_out, out_3[7]);
  and and_36 (and_36_out, and_35_out, not_15_out);
  and and_37 (and_37_out, out_3[7], and_35_out);
  J_K_Flip_Flop j_k_ff_8 (
    .J(and_36_out), .clk(in_1), .K(and_37_out), .Q(out_3[7]), .preset(and_38_out), .reset(and_39_out));  // open: Qn, en
  and and_38 (and_38_out, in_2[7], Setter);
  not not_16 (not_16_out, in_2[7]);
  and and_39 (and_39_out, not_16_out, Setter);
  or or_1 (Setter, in_2[0], in_2[1], in_2[2], in_2[3], in_2[4], in_2[5], in_2[6], in_2[7]);
  and and_40 (pulso8, and_35_out, out_3[7]);

  // Other names for the same wires on the sheet: c = in_1; e1 = in_2[0]; e2 = in_2[1]; e3 = in_2[2]; e4 = in_2[3];
  //   e5 = in_2[4]; e6 = in_2[5]; e7 = in_2[6]; e8 = in_2[7]; s1 = out_3[0]; s2 = out_3[1]; s3 = out_3[2];
  //   s4 = out_3[3]; s5 = out_3[4]; s6 = out_3[5]; s7 = out_3[6]; s8 = out_3[7]
endmodule

module Controlador (
  input  [15:0] \Conteúdo_do_IR ,
  input  in_2,
  output Memory_out_in,
  output IR_out_in,
  output PC_plus_plus
);

  wire and_2_out, and_3_out, and_6_out, and_7_out, and_8_out, and_10_out, est0, est2, est3, not_1_out,
       not_2_out, not_3_out, not_4_out, not_5_out, s1, s2;

  not not_1 (not_1_out, s1);
  not not_2 (not_2_out, s2);
  and and_1 (est0, not_2_out, not_1_out);
  not not_3 (not_3_out, s1);
  and and_2 (and_2_out, 1'b1, not_3_out);
  and and_3 (and_3_out, 1'b1, s1);
  J_K_Flip_Flop j_k_ff_1 (.J(and_2_out), .clk(in_2), .K(and_3_out), .Q(s1));  // open: Qn, preset, en, reset
  and and_4 (PC_plus_plus, s1, not_2_out);
  and and_5 (est2, s2, not_1_out);
  and and_6 (and_6_out, 1'b1, s1);
  not not_4 (not_4_out, s2);
  and and_7 (and_7_out, and_6_out, not_4_out);
  and and_8 (and_8_out, s2, and_6_out);
  and and_9 (est3, s2, s1);
  J_K_Flip_Flop j_k_ff_2 (.J(and_7_out), .clk(in_2), .K(and_8_out), .Q(s2));  // open: Qn, preset, en, reset
  and and_10 (and_10_out, and_6_out, s2);
  not not_5 (not_5_out, PC_plus_plus);
  or or_1 (IR_out_in, est0, not_5_out);
  nand nand_1 (Memory_out_in, PC_plus_plus, est0);

  // Other names for the same wires on the sheet: c = in_2; est1 = PC_plus_plus

  // Notes on the sheet:
  //   Estado 0
  //   Estado 1
  //   Estado 2
  //   Estado 3
endmodule

module Main (
);

  wire Clock, controlador_1_ir_out_in, controlador_1_memory_out_in, controlador_1_pc_plus_plus;
  wire [7:0] \dário_1_out_3 ;
  wire [15:0] ACC_q, IR_q, ram_1_data;

  RAM #(.dataWidth(16)) ram_1 (
    .addr(\dário_1_out_3 ), .data(ram_1_data), .clk(Clock), .ld(controlador_1_memory_out_in));  // open: sel, clr
  Clock clock_1 (.out(Clock));
  Controlador controlador_1 (
    .Memory_out_in(controlador_1_memory_out_in), .IR_out_in(controlador_1_ir_out_in),
    .\Conteúdo_do_IR (IR_q), .PC_plus_plus(controlador_1_pc_plus_plus), .in_2(Clock));
  \Dário  \dário_1  (.out_3(\dário_1_out_3 ), .in_1(controlador_1_pc_plus_plus));  // open: in_2
  Register #(.width(16)) IR (.D(ram_1_data), .Q(IR_q), .clk(controlador_1_ir_out_in));  // open: en, clr
  Register #(.width(16)) ACC (.Q(ACC_q));  // open: D, en, clk, clr
  Controlled_Buffer #(.width(16)) controlled_buffer_1 (.in(ACC_q));  // open: out, en
endmodule
